// Logisim project shared-memory.circ as structural Verilog: 3 circuits, main circuit shared-memory-main
module shared_memory_main (
);

  wire [31:0] n2x32x32bit_combiner_1_out_65, n2x32x32bit_combiner_1_out_66, n2x32x32bit_combiner_1_out_67,
       n2x32x32bit_combiner_1_out_68, n2x32x32bit_combiner_1_out_69, n2x32x32bit_combiner_1_out_70,
       n2x32x32bit_combiner_1_out_71, n2x32x32bit_combiner_1_out_72, n2x32x32bit_combiner_1_out_73,
       n2x32x32bit_combiner_1_out_74, n2x32x32bit_combiner_1_out_75, n2x32x32bit_combiner_1_out_76,
       n2x32x32bit_combiner_1_out_77, n2x32x32bit_combiner_1_out_78, n2x32x32bit_combiner_1_out_79,
       n2x32x32bit_combiner_1_out_80, n2x32x32bit_combiner_1_out_81, n2x32x32bit_combiner_1_out_82,
       n2x32x32bit_combiner_1_out_83, n2x32x32bit_combiner_1_out_84, n2x32x32bit_combiner_1_out_85,
       n2x32x32bit_combiner_1_out_86, n2x32x32bit_combiner_1_out_87, n2x32x32bit_combiner_1_out_88,
       n2x32x32bit_combiner_1_out_89, n2x32x32bit_combiner_1_out_90, n2x32x32bit_combiner_1_out_91,
       n2x32x32bit_combiner_1_out_92, n2x32x32bit_combiner_1_out_93, n2x32x32bit_combiner_1_out_95,
       n2x32x32bit_combiner_1_out_96, n32bit_screen_buffer_1_out_1, n32bit_screen_buffer_1_out_2,
       n32bit_screen_buffer_1_out_3, n32bit_screen_buffer_1_out_4, n32bit_screen_buffer_1_out_5,
       n32bit_screen_buffer_1_out_6, n32bit_screen_buffer_1_out_7, n32bit_screen_buffer_1_out_8,
       n32bit_screen_buffer_1_out_9, n32bit_screen_buffer_1_out_10, n32bit_screen_buffer_1_out_11,
       n32bit_screen_buffer_1_out_12, n32bit_screen_buffer_1_out_13, n32bit_screen_buffer_1_out_14,
       n32bit_screen_buffer_1_out_15, n32bit_screen_buffer_1_out_17, n32bit_screen_buffer_1_out_18,
       n32bit_screen_buffer_1_out_19, n32bit_screen_buffer_1_out_20, n32bit_screen_buffer_1_out_21,
       n32bit_screen_buffer_1_out_22, n32bit_screen_buffer_1_out_23, n32bit_screen_buffer_1_out_24,
       n32bit_screen_buffer_1_out_25, n32bit_screen_buffer_1_out_26, n32bit_screen_buffer_1_out_27,
       n32bit_screen_buffer_1_out_28, n32bit_screen_buffer_1_out_29, n32bit_screen_buffer_1_out_30,
       n32bit_screen_buffer_1_out_31, n32bit_screen_buffer_1_out_32;

  _32bit_screen_buffer u_32bit_screen_buffer_1 (
    .out_1(n32bit_screen_buffer_1_out_1), .out_2(n32bit_screen_buffer_1_out_2),
    .out_3(n32bit_screen_buffer_1_out_3), .out_4(n32bit_screen_buffer_1_out_4),
    .out_5(n32bit_screen_buffer_1_out_5), .out_6(n32bit_screen_buffer_1_out_6),
    .out_7(n32bit_screen_buffer_1_out_7), .out_8(n32bit_screen_buffer_1_out_8),
    .out_9(n32bit_screen_buffer_1_out_9), .out_10(n32bit_screen_buffer_1_out_10),
    .out_11(n32bit_screen_buffer_1_out_11), .out_12(n32bit_screen_buffer_1_out_12),
    .out_13(n32bit_screen_buffer_1_out_13), .out_14(n32bit_screen_buffer_1_out_14),
    .out_15(n32bit_screen_buffer_1_out_15), .out_16(n32bit_screen_buffer_1_out_15),
    .out_17(n32bit_screen_buffer_1_out_17), .out_18(n32bit_screen_buffer_1_out_18),
    .out_19(n32bit_screen_buffer_1_out_19), .out_20(n32bit_screen_buffer_1_out_20),
    .out_21(n32bit_screen_buffer_1_out_21), .out_22(n32bit_screen_buffer_1_out_22),
    .out_23(n32bit_screen_buffer_1_out_23), .out_24(n32bit_screen_buffer_1_out_24),
    .out_25(n32bit_screen_buffer_1_out_25), .out_26(n32bit_screen_buffer_1_out_26),
    .out_27(n32bit_screen_buffer_1_out_27), .out_28(n32bit_screen_buffer_1_out_28),
    .out_29(n32bit_screen_buffer_1_out_29), .out_30(n32bit_screen_buffer_1_out_30),
    .out_31(n32bit_screen_buffer_1_out_31), .out_32(n32bit_screen_buffer_1_out_32));
  _2x32x32bit_combiner u_2x32x32bit_combiner_1 (
    .in_1(n32bit_screen_buffer_1_out_1), .in_2(n32bit_screen_buffer_1_out_2),
    .in_3(n32bit_screen_buffer_1_out_3), .in_4(n32bit_screen_buffer_1_out_4),
    .in_5(n32bit_screen_buffer_1_out_5), .in_6(n32bit_screen_buffer_1_out_6),
    .in_7(n32bit_screen_buffer_1_out_7), .in_8(n32bit_screen_buffer_1_out_8),
    .in_9(n32bit_screen_buffer_1_out_9), .in_10(n32bit_screen_buffer_1_out_10),
    .in_11(n32bit_screen_buffer_1_out_11), .in_12(n32bit_screen_buffer_1_out_12),
    .in_13(n32bit_screen_buffer_1_out_13), .in_14(n32bit_screen_buffer_1_out_14),
    .in_15(n32bit_screen_buffer_1_out_15), .in_16(n32bit_screen_buffer_1_out_15),
    .in_17(n32bit_screen_buffer_1_out_17), .in_18(n32bit_screen_buffer_1_out_18),
    .in_19(n32bit_screen_buffer_1_out_19), .in_20(n32bit_screen_buffer_1_out_20),
    .in_21(n32bit_screen_buffer_1_out_21), .in_22(n32bit_screen_buffer_1_out_22),
    .in_23(n32bit_screen_buffer_1_out_23), .in_24(n32bit_screen_buffer_1_out_24),
    .in_25(n32bit_screen_buffer_1_out_25), .in_26(n32bit_screen_buffer_1_out_26),
    .in_27(n32bit_screen_buffer_1_out_27), .in_28(n32bit_screen_buffer_1_out_28),
    .in_29(n32bit_screen_buffer_1_out_29), .in_30(n32bit_screen_buffer_1_out_30),
    .in_31(n32bit_screen_buffer_1_out_31), .in_32(n32bit_screen_buffer_1_out_32),
    .out_65(n2x32x32bit_combiner_1_out_65), .out_66(n2x32x32bit_combiner_1_out_66),
    .out_67(n2x32x32bit_combiner_1_out_67), .out_68(n2x32x32bit_combiner_1_out_68),
    .out_69(n2x32x32bit_combiner_1_out_69), .out_70(n2x32x32bit_combiner_1_out_70),
    .out_71(n2x32x32bit_combiner_1_out_71), .out_72(n2x32x32bit_combiner_1_out_72),
    .out_73(n2x32x32bit_combiner_1_out_73), .out_74(n2x32x32bit_combiner_1_out_74),
    .out_75(n2x32x32bit_combiner_1_out_75), .out_76(n2x32x32bit_combiner_1_out_76),
    .out_77(n2x32x32bit_combiner_1_out_77), .out_78(n2x32x32bit_combiner_1_out_78),
    .out_79(n2x32x32bit_combiner_1_out_79), .out_80(n2x32x32bit_combiner_1_out_80),
    .out_81(n2x32x32bit_combiner_1_out_81), .out_82(n2x32x32bit_combiner_1_out_82),
    .out_83(n2x32x32bit_combiner_1_out_83), .out_84(n2x32x32bit_combiner_1_out_84),
    .out_85(n2x32x32bit_combiner_1_out_85), .out_86(n2x32x32bit_combiner_1_out_86),
    .out_87(n2x32x32bit_combiner_1_out_87), .out_88(n2x32x32bit_combiner_1_out_88),
    .out_89(n2x32x32bit_combiner_1_out_89), .out_90(n2x32x32bit_combiner_1_out_90),
    .out_91(n2x32x32bit_combiner_1_out_91), .out_92(n2x32x32bit_combiner_1_out_92),
    .out_93(n2x32x32bit_combiner_1_out_93), .out_94(n2x32x32bit_combiner_1_out_93),
    .out_95(n2x32x32bit_combiner_1_out_95), .out_96(n2x32x32bit_combiner_1_out_96));  // open: in_33, in_34, in_35, in_36, in_37, in_38, in_39, in_40, in_41, in_42, in_43, in_44, in_45, in_46, in_47, in_48, in_49, in_50, in_51, in_52, in_53, in_54, in_55, in_56, in_57, in_58, in_59, in_60, in_61, in_62, in_63, in_64
  _32bit_screen_buffer u_32bit_screen_buffer_2 ();  // open: out_1, out_2, out_3, out_4, out_5, out_6, out_7, out_8, out_9, out_10, out_11, out_12, out_13, out_14, out_15, out_16, out_17, out_18, out_19, out_20, out_21, out_22, out_23, out_24, out_25, out_26, out_27, out_28, out_29, out_30, out_31, out_32
  DotMatrix #(.inputtype("row"), .matrixcols(32), .matrixrows(32)) dotmatrix_1 (
    .row0(n2x32x32bit_combiner_1_out_65), .row1(n2x32x32bit_combiner_1_out_66),
    .row2(n2x32x32bit_combiner_1_out_67), .row3(n2x32x32bit_combiner_1_out_68),
    .row4(n2x32x32bit_combiner_1_out_69), .row5(n2x32x32bit_combiner_1_out_70),
    .row6(n2x32x32bit_combiner_1_out_71), .row7(n2x32x32bit_combiner_1_out_72),
    .row8(n2x32x32bit_combiner_1_out_73), .row9(n2x32x32bit_combiner_1_out_74),
    .row10(n2x32x32bit_combiner_1_out_75), .row11(n2x32x32bit_combiner_1_out_76),
    .row12(n2x32x32bit_combiner_1_out_77), .row13(n2x32x32bit_combiner_1_out_78),
    .row14(n2x32x32bit_combiner_1_out_79), .row15(n2x32x32bit_combiner_1_out_80),
    .row16(n2x32x32bit_combiner_1_out_81), .row17(n2x32x32bit_combiner_1_out_82),
    .row18(n2x32x32bit_combiner_1_out_83), .row19(n2x32x32bit_combiner_1_out_84),
    .row20(n2x32x32bit_combiner_1_out_85), .row21(n2x32x32bit_combiner_1_out_86),
    .row22(n2x32x32bit_combiner_1_out_87), .row23(n2x32x32bit_combiner_1_out_88),
    .row24(n2x32x32bit_combiner_1_out_89), .row25(n2x32x32bit_combiner_1_out_90),
    .row26(n2x32x32bit_combiner_1_out_91), .row27(n2x32x32bit_combiner_1_out_92),
    .row28(n2x32x32bit_combiner_1_out_93), .row29(n2x32x32bit_combiner_1_out_93),
    .row30(n2x32x32bit_combiner_1_out_95), .row31(n2x32x32bit_combiner_1_out_96));
endmodule

module _32bit_screen_buffer (
  output [31:0] out_1,
  output [31:0] out_2,
  output [31:0] out_3,
  output [31:0] out_4,
  output [31:0] out_5,
  output [31:0] out_6,
  output [31:0] out_7,
  output [31:0] out_8,
  output [31:0] out_9,
  output [31:0] out_10,
  output [31:0] out_11,
  output [31:0] out_12,
  output [31:0] out_13,
  output [31:0] out_14,
  output [31:0] out_15,
  output [31:0] out_16,
  output [31:0] out_17,
  output [31:0] out_18,
  output [31:0] out_19,
  output [31:0] out_20,
  output [31:0] out_21,
  output [31:0] out_22,
  output [31:0] out_23,
  output [31:0] out_24,
  output [31:0] out_25,
  output [31:0] out_26,
  output [31:0] out_27,
  output [31:0] out_28,
  output [31:0] out_29,
  output [31:0] out_30,
  output [31:0] out_31,
  output [31:0] out_32
);
endmodule

module _2x32x32bit_combiner (
  input  [31:0] in_1,
  input  [31:0] in_2,
  input  [31:0] in_3,
  input  [31:0] in_4,
  input  [31:0] in_5,
  input  [31:0] in_6,
  input  [31:0] in_7,
  input  [31:0] in_8,
  input  [31:0] in_9,
  input  [31:0] in_10,
  input  [31:0] in_11,
  input  [31:0] in_12,
  input  [31:0] in_13,
  input  [31:0] in_14,
  input  [31:0] in_15,
  input  [31:0] in_16,
  input  [31:0] in_17,
  input  [31:0] in_18,
  input  [31:0] in_19,
  input  [31:0] in_20,
  input  [31:0] in_21,
  input  [31:0] in_22,
  input  [31:0] in_23,
  input  [31:0] in_24,
  input  [31:0] in_25,
  input  [31:0] in_26,
  input  [31:0] in_27,
  input  [31:0] in_28,
  input  [31:0] in_29,
  input  [31:0] in_30,
  input  [31:0] in_31,
  input  [31:0] in_32,
  input  [31:0] in_33,
  input  [31:0] in_34,
  input  [31:0] in_35,
  input  [31:0] in_36,
  input  [31:0] in_37,
  input  [31:0] in_38,
  input  [31:0] in_39,
  input  [31:0] in_40,
  input  [31:0] in_41,
  input  [31:0] in_42,
  input  [31:0] in_43,
  input  [31:0] in_44,
  input  [31:0] in_45,
  input  [31:0] in_46,
  input  [31:0] in_47,
  input  [31:0] in_48,
  input  [31:0] in_49,
  input  [31:0] in_50,
  input  [31:0] in_51,
  input  [31:0] in_52,
  input  [31:0] in_53,
  input  [31:0] in_54,
  input  [31:0] in_55,
  input  [31:0] in_56,
  input  [31:0] in_57,
  input  [31:0] in_58,
  input  [31:0] in_59,
  input  [31:0] in_60,
  input  [31:0] in_61,
  input  [31:0] in_62,
  input  [31:0] in_63,
  input  [31:0] in_64,
  output [31:0] out_65,
  output [31:0] out_66,
  output [31:0] out_67,
  output [31:0] out_68,
  output [31:0] out_69,
  output [31:0] out_70,
  output [31:0] out_71,
  output [31:0] out_72,
  output [31:0] out_73,
  output [31:0] out_74,
  output [31:0] out_75,
  output [31:0] out_76,
  output [31:0] out_77,
  output [31:0] out_78,
  output [31:0] out_79,
  output [31:0] out_80,
  output [31:0] out_81,
  output [31:0] out_82,
  output [31:0] out_83,
  output [31:0] out_84,
  output [31:0] out_85,
  output [31:0] out_86,
  output [31:0] out_87,
  output [31:0] out_88,
  output [31:0] out_89,
  output [31:0] out_90,
  output [31:0] out_91,
  output [31:0] out_92,
  output [31:0] out_93,
  output [31:0] out_94,
  output [31:0] out_95,
  output [31:0] out_96
);


  assign in_33 = in_1;
  assign in_34 = in_2;
  assign in_35 = in_3;
  assign in_36 = in_4;
  assign in_37 = in_5;
  assign in_38 = in_6;
  assign in_39 = in_7;
  assign in_40 = in_8;
  assign in_41 = in_9;
  assign in_42 = in_10;
  assign in_43 = in_11;
  assign in_44 = in_12;
  assign in_45 = in_13;
  assign in_46 = in_14;
  assign in_47 = in_15;
  assign in_48 = in_16;
  assign in_49 = in_17;
  assign in_50 = in_18;
  assign in_51 = in_19;
  assign in_52 = in_20;
  assign in_53 = in_21;
  assign in_54 = in_22;
  assign in_55 = in_23;
  assign in_56 = in_24;
  assign in_57 = in_25;
  assign in_58 = in_26;
  assign in_59 = in_27;
  assign in_60 = in_28;
  assign in_61 = in_29;
  assign in_62 = in_30;
  assign in_63 = in_31;
  assign in_64 = in_32;
  assign out_65 = in_1;
  assign out_66 = in_2;
  assign out_67 = in_3;
  assign out_68 = in_4;
  assign out_69 = in_5;
  assign out_70 = in_6;
  assign out_71 = in_7;
  assign out_72 = in_8;
  assign out_73 = in_9;
  assign out_74 = in_10;
  assign out_75 = in_11;
  assign out_76 = in_12;
  assign out_77 = in_13;
  assign out_78 = in_14;
  assign out_79 = in_15;
  assign out_80 = in_16;
  assign out_81 = in_17;
  assign out_82 = in_18;
  assign out_83 = in_19;
  assign out_84 = in_20;
  assign out_85 = in_21;
  assign out_86 = in_22;
  assign out_87 = in_23;
  assign out_88 = in_24;
  assign out_89 = in_25;
  assign out_90 = in_26;
  assign out_91 = in_27;
  assign out_92 = in_28;
  assign out_93 = in_29;
  assign out_94 = in_30;
  assign out_95 = in_31;
  assign out_96 = in_32;
endmodule
